# Fritzing sketch Q0211-Esquema - Parte Final (saved by Fritzing 0.9.3b)
circuit board: 13.418cm x 9.62053cm
breadboards: 9

parts:
  U1 = 74HC595 [package="DIP16 [THT]"]
  IN = male pin header, 5 pins [form="♂ (male)"]
  5V = Power plug
  R1 = Resistor [tolerance=±5% resistance=1k package=THT]
  Q1 = NPN-Transistor [package="TO92 [THT]"]
  D1 = Rectifier Diode [part_number=1N4007 package="300 mil [THT]"]
  R9 = Resistor [tolerance=±5% resistance=220 package=THT]
  LED1 = LED - 3mm [color="Red (633nm)" package="3 mm [THT]"]
  RL1 = Rele Generico [package=relay-g5q]
  R2 = Resistor [tolerance=±5% resistance=1k package=THT]
  Q2 = NPN-Transistor [package="TO92 [THT]"]
  D2 = Rectifier Diode [part_number=1N4007 package="300 mil [THT]"]
  R10 = Resistor [tolerance=±5% resistance=220 package=THT]
  LED2 = LED - 3mm [color="Red (633nm)" package="3 mm [THT]"]
  RL2 = Rele Generico [package=relay-g5q]
  R3 = Resistor [tolerance=±5% resistance=1k package=THT]
  R4 = Resistor [tolerance=±5% resistance=1k package=THT]
  Q3 = NPN-Transistor [package="TO92 [THT]"]
  Q4 = NPN-Transistor [package="TO92 [THT]"]
  D3 = Rectifier Diode [part_number=1N4007 package="300 mil [THT]"]
  D4 = Rectifier Diode [part_number=1N4007 package="300 mil [THT]"]
  R11 = Resistor [tolerance=±5% resistance=220 package=THT]
  R12 = Resistor [tolerance=±5% resistance=220 package=THT]
  LED3 = LED - 3mm [color="Red (633nm)" package="3 mm [THT]"]
  LED4 = LED - 3mm [color="Red (633nm)" package="3 mm [THT]"]
  RL3 = Rele Generico [package=relay-g5q]
  RL4 = Rele Generico [package=relay-g5q]
  R5 = Resistor [tolerance=±5% resistance=1k package=THT]
  R8 = Resistor [tolerance=±5% resistance=1k package=THT]
  R7 = Resistor [tolerance=±5% resistance=1k package=THT]
  R6 = Resistor [tolerance=±5% resistance=1k package=THT]
  Q5 = NPN-Transistor [package="TO92 [THT]"]
  Q8 = NPN-Transistor [package="TO92 [THT]"]
  Q7 = NPN-Transistor [package="TO92 [THT]"]
  Q6 = NPN-Transistor [package="TO92 [THT]"]
  D5 = Rectifier Diode [part_number=1N4007 package="300 mil [THT]"]
  D8 = Rectifier Diode [part_number=1N4007 package="300 mil [THT]"]
  D7 = Rectifier Diode [part_number=1N4007 package="300 mil [THT]"]
  D6 = Rectifier Diode [part_number=1N4007 package="300 mil [THT]"]
  R13 = Resistor [tolerance=±5% resistance=220 package=THT]
  R14 = Resistor [tolerance=±5% resistance=220 package=THT]
  R16 = Resistor [tolerance=±5% resistance=220 package=THT]
  R15 = Resistor [tolerance=±5% resistance=220 package=THT]
  LED5 = LED - 3mm [color="Red (633nm)" package="3 mm [THT]"]
  LED8 = LED - 3mm [color="Red (633nm)" package="3 mm [THT]"]
  LED6 = LED - 3mm [color="Red (633nm)" package="3 mm [THT]"]
  LED7 = LED - 3mm [color="Red (633nm)" package="3 mm [THT]"]
  RL5 = Rele Generico [package=relay-g5q]
  RL6 = Rele Generico [package=relay-g5q]
  RL7 = Rele Generico [package=relay-g5q]
  RL8 = Rele Generico [package=relay-g5q]
  OUT = female pin header, 5 pins [form="♀ (female)"]
  J1 = screw terminal, 3 pins
  J2 = screw terminal, 3 pins
  J3 = screw terminal, 3 pins
  J4 = screw terminal, 3 pins
  J5 = screw terminal, 3 pins
  J6 = screw terminal, 3 pins
  J7 = screw terminal, 3 pins
  J8 = screw terminal, 3 pins

nets:
  Canal 2: U1.Q1, R2.Pin_0
  Canal 3: U1.Q2, R3.Pin_0
  Canal 4: U1.Q3, R4.Pin_0
  Canal 5: U1.Q4, R5.Pin_0
  Canal 6: U1.Q5, R6.Pin_0
  Canal 7: U1.Q6, R7.Pin_0
  Canal 8: U1.Q7, R8.Pin_0
  GND: U1.GND, U1.OE, IN.pin1, 5V.GND, D1.anode, R9.Pin_0, RL1.BOBINA1, D2.anode, R10.Pin_0, RL2.BOBINA1, D3.anode, D4.anode, R11.Pin_0, R12.Pin_0, RL3.BOBINA1, RL4.BOBINA1, D5.anode, D8.anode, D7.anode, D6.anode, R13.Pin_0, R14.Pin_0, R16.Pin_0, R15.Pin_0, RL5.BOBINA1, RL6.BOBINA1, RL7.BOBINA1, RL8.BOBINA1, OUT.pin1
  DATA OUT: U1.Q7', OUT.pin2
  5V: U1.MR, U1.VCC, IN.pin5, 5V.VCC, Q1.C, Q2.C, Q3.C, Q4.C, Q5.C, Q8.C, Q7.C, Q6.C, OUT.pin5
  CLK: U1.SH_CP, IN.pin4, OUT.pin4
  LATCH: U1.ST_CP, IN.pin3, OUT.pin3
  DATA IN: U1.DS, IN.pin2
  Canal 1: U1.Q0, R1.Pin_0
  N1: R1.Pin_1, Q1.B
  N2: Q1.E, D1.cathode, LED1.anode, RL1.BOBINA2
  N3: R9.Pin_1, LED1.cathode
  N4: RL1.ENTRADA, J1.pin2
  N5: RL1.NA, J1.pin3
  N6: RL1.NF, J1.pin1
  N7: R2.Pin_1, Q2.B
  N8: Q2.E, D2.cathode, LED2.anode, RL2.BOBINA2
  N9: R10.Pin_1, LED2.cathode
  N10: RL2.ENTRADA, J2.pin2
  N11: RL2.NA, J2.pin3
  N12: RL2.NF, J2.pin1
  N13: R3.Pin_1, Q3.B
  N14: R4.Pin_1, Q4.B
  N15: Q3.E, D3.cathode, LED3.anode, RL3.BOBINA2
  N16: Q4.E, D4.cathode, LED4.anode, RL4.BOBINA2
  N17: R11.Pin_1, LED3.cathode
  N18: R12.Pin_1, LED4.cathode
  N19: RL3.ENTRADA, J3.pin2
  N20: RL3.NA, J3.pin3
  N21: RL3.NF, J3.pin1
  N22: RL4.ENTRADA, J4.pin2
  N23: RL4.NA, J4.pin3
  N24: RL4.NF, J4.pin1
  N25: R5.Pin_1, Q5.B
  N26: R8.Pin_1, Q8.B
  N27: R7.Pin_1, Q7.B
  N28: R6.Pin_1, Q6.B
  N29: Q5.E, D5.cathode, LED5.anode, RL5.BOBINA2
  N30: Q8.E, D8.cathode, LED8.anode, RL8.BOBINA2
  N31: Q7.E, D7.cathode, LED7.anode, RL7.BOBINA2
  N32: Q6.E, D6.cathode, LED6.anode, RL6.BOBINA2
  N33: R13.Pin_1, LED5.cathode
  N34: R14.Pin_1, LED6.cathode
  N35: R16.Pin_1, LED8.cathode
  N36: R15.Pin_1, LED7.cathode
  N37: RL5.ENTRADA, J5.pin2
  N38: RL5.NA, J5.pin3
  N39: RL5.NF, J5.pin1
  N40: RL6.ENTRADA, J6.pin2
  N41: RL6.NA, J6.pin3
  N42: RL6.NF, J6.pin1
  N43: RL7.ENTRADA, J7.pin2
  N44: RL7.NA, J7.pin3
  N45: RL7.NF, J7.pin1
  N46: RL8.ENTRADA, J8.pin2
  N47: RL8.NA, J8.pin3
  N48: RL8.NF, J8.pin1

custom parts:
  Rele Generico: MPA-S-105-C
